# Fritzing sketch diagramESP32 (saved by Fritzing 0.9.3b)

parts:
  BAT1 = Battery Holders [package=battery-aaa]
  Mod1 = KY-019 5V Relay Module [package="Breakout board"]
  M1 = DC Motor
  U1 = ESP32-38PinWide [part_number=ESP32-38PinWide]

nets:
  N1: BAT1.-, M1.pin_1
  N2: BAT1.+, Mod1.Common
  N3: Mod1.S, U1.GPIO5
  N4: Mod1.+, U1.VIN
  N5: Mod1.-, U1.GPIO11
  N6: Mod1.NO, M1.pin_2

custom parts:
  KY-019 5V Relay Module: KY-019 5V Relay module, used to control AC circuits.
  ESP32-38PinWide: Generic 38-Pin ESP32 with wide format (only access to one side of pins on a breadboard) based on Stephen Lilley's HiLetgo ESP-WROOM-32 ESP32 ESP-32S Development Board.
