# Fritzing sketch diagramUNO (saved by Fritzing 0.9.3b)

parts:
  Part1 = Arduino Uno (Rev3) - ICSP
  BAT1 = Battery Holders [package=battery-aaa]
  Mod1 = KY-019 5V Relay Module [package="Breakout board"]
  M1 = DC Motor

nets:
  N1: Part1.D7, Mod1.S
  N2: Part1.5V, Mod1.+
  N3: Part1.GND, Mod1.-
  N4: BAT1.-, M1.pin_1
  N5: BAT1.+, Mod1.Common
  N6: Mod1.NO, M1.pin_2

custom parts:
  KY-019 5V Relay Module: KY-019 5V Relay module, used to control AC circuits.
